# Fritzing sketch Moteur (saved by Fritzing 0.9.1b)

parts:
  Composant1 = Arduino Uno (Rev3)  # not connected
  Composant2 = Arduino Motor Shield (Rev3)
  M1 = DC Motor
  VCC1 = Battery

nets:
  N1: Composant2.B-, M1.pin_2
  N2: Composant2.B+, M1.pin_1
  N3: Composant2.VMOT, VCC1.+
  N4: Composant2.GND, VCC1.-
