# Fritzing sketch Potentiomètre (saved by Fritzing 0.9.1b)
circuit board: 8.46667cm x 5.64444cm

parts:
  Composant1 = Arduino Uno (Rev3)
  R1 = Rotary Potentiometer (Small) [maximum_resistance=47kΩ package=THT]

nets:
  N1: Composant1.A5/SCL, R1.wiper
  N2: Composant1.5V, R1.leg2
  N3: Composant1.GND, R1.leg1
