# Fritzing sketch cablage2 (saved by Fritzing 0.9.3b)

parts:
  Composant1 = Arduino Mega ADK (Rev3)
  Composant2 = Triple Axis Accelerometer Breakout - ADXL335
  J1 = Basic Servo

nets:
  N1: Composant1.A1, Composant2.XOUT
  GND: Composant1.GND, Composant2.GND, J1.gnd
  N2: Composant1.D9_PWM, J1.pulse
  3V3: Composant1.3V3, Composant2.VCC
  5V: Composant1.5V, J1.vcc
